# Fritzing sketch RotaryEncoderRGB_Sparkfun_debouncing_board (saved by Fritzing 0.9.3b)
circuit board: 5cm x 3cm
breadboards: 1

parts:
  R3 = Resistor [tolerance=±5% resistance=10k package=THT]
  R2 = Resistor [tolerance=±5% resistance=10k package=THT]
  R4 = Resistor [tolerance=±5% resistance=10k package=THT]
  R1 = Resistor [tolerance=±5% resistance=10k package=THT]
  C2 = Ceramic Capacitor [capacitance=100nF package="100 mil [THT, multilayer]"]
  C1 = Ceramic Capacitor [capacitance=100nF package="100 mil [THT, multilayer]"]
  R5 = Resistor [tolerance=±5% resistance=10k package=THT]
  R6 = Resistor [tolerance=±5% resistance=100 package=THT]
  R7 = Resistor [tolerance=±5% resistance=100 package=THT]
  R8 = Resistor [tolerance=±5% resistance=150 package=THT]
  SW1 = ENCODER_RGB_CA [package=encoder_led_3]
  C3 = Ceramic Capacitor [capacitance=100nF package="100 mil [THT, multilayer]"]
  J2 = male pin header, 6 pins [form="♂ (male)"]
  3_3-5V = male pin header, 2 pins [form="♂ (male)"]

nets:
  5V: R3.Pin_0, R2.Pin_0, SW1.+, C3.1, 3_3-5V.pin1
  N1: R3.Pin_1, R4.Pin_1, SW1.A
  N2: R2.Pin_1, R1.Pin_1, SW1.B
  N3: R4.Pin_0, C2.1, J2.pin6
  N4: R1.Pin_0, C1.1, J2.pin5
  GND: C2.0, C1.0, R5.Pin_1, SW1.C, 3_3-5V.pin2
  N5: R5.Pin_0, SW1.SW, C3.0, J2.pin4
  N6: R6.Pin_0, SW1.-B
  N7: R6.Pin_1, J2.pin3
  N8: R7.Pin_0, SW1.-G
  N9: R7.Pin_1, J2.pin2
  N10: R8.Pin_0, SW1.-R
  N11: R8.Pin_1, J2.pin1

notes:
  - +
  12 S BGR
  debouncer
  GND
  +5V
  output
