# Fritzing sketch RotaryEncoderRGB_Sparkfun_debouncing_board_SMD_footprint (saved by Fritzing 0.9.3b)
circuit board: 3.5cm x 3cm
breadboards: 1

parts:
  C2 = Ceramic Capacitor [capacitance=100nF package="100 mil [THT, multilayer]"]
  C1 = Ceramic Capacitor [capacitance=100nF package="100 mil [THT, multilayer]"]
  J2 = female pin header, 6 pins [form="♀ (female)"]
  3-5V = female pin header, 2 pins [form="♀ (female)"]
  SW1 = ENCODER_RGB_CA [package=encoder_led_3]
  C3 = Ceramic Capacitor [capacitance=100nF package="100 mil [THT, multilayer]"]
  R4 = Resistor [tolerance=±5% resistance=10k package="1206 [SMD]"]
  R3 = Resistor [tolerance=±5% resistance=10k package="1206 [SMD]"]
  R2 = Resistor [tolerance=±5% resistance=10k package="1206 [SMD]"]
  R8 = Resistor [tolerance=±5% resistance=150 package="1206 [SMD]"]
  R7 = Resistor [tolerance=±5% resistance=100 package="1206 [SMD]"]
  R6 = Resistor [tolerance=±5% resistance=100 package="1206 [SMD]"]
  R5 = Resistor [tolerance=±5% resistance=10k package="1206 [SMD]"]
  R1 = Resistor [tolerance=±5% resistance=10k package="1206 [SMD]"]

nets:
  GND: C2.0, C1.0, 3-5V.pin2, SW1.C, R5.Pin_1
  N1: C2.1, J2.pin6, R4.Pin_0
  N2: C1.1, J2.pin5, R1.Pin_0
  N3: J2.pin1, R8.Pin_1
  N4: J2.pin2, R7.Pin_1
  N5: J2.pin3, R6.Pin_1
  N6: J2.pin4, SW1.SW, C3.0, R5.Pin_0
  5V: 3-5V.pin1, SW1.+, C3.1, R3.Pin_0, R2.Pin_0
  N7: SW1.-R, R8.Pin_0
  N8: SW1.-G, R7.Pin_0
  N9: SW1.-B, R6.Pin_0
  N10: SW1.A, R4.Pin_1, R3.Pin_1
  N11: SW1.B, R2.Pin_1, R1.Pin_1

notes:
  - +
  12 S BGR
  Debouncer
  GND
  +5V
  output
